# Fritzing sketch Windows_doors_switch (saved by Fritzing 0.8.3b)
breadboards: 1

parts:
  IC1 = MCP23017 I2C I/O Expander
  Raspberry_Pi_rev1 = Raspberry Pi rev2
  S1 = Square Pushbutton
  S2 = Square Pushbutton

nets:
  VSS: IC1.VSS, IC1.A2, IC1.RESET, Raspberry_Pi_rev1.5V, S1.leg0, S2.leg1
  N1: IC1.NC#11, IC1.A0, IC1.A1, Raspberry_Pi_rev1.GND
  N2: IC1.SCL, Raspberry_Pi_rev1.GIPO_3
  N3: IC1.SDA, Raspberry_Pi_rev1.GIPO_2
  N4: IC1.GPA1, S2.leg0
  N5: IC1.GPA3, S1.leg1

custom parts:
  MCP23017 I2C I/O Expander: MCP23017 I2C 16-Channel I/O Expander
